# Fritzing sketch VMC (saved by Fritzing 0.9.3b)
breadboards: 1

parts:
  Composant1 = Photon
  PIR1 = PIR sensor
  DHT1 = DHT22 Humidity and Temperature Sensor
  R1 = Resistor [tolerance=±5% resistance=10k package=THT]
  LDR = Photocell (LDR) [package=THT]
  PC_Fan = polarizedheader 4pin 0.156in [package=THT]
  R3 = Resistor [tolerance=±5% resistance=10k package=THT]
  R2 = Resistor [tolerance=±5% resistance=10k package=THT]
  M1 = RioRand LM2596
  Composant2 = ws2812b [package="smd 2812b"]

nets:
  N1: Composant1.A0, LDR.pin_0, R3.Pin_0
  N2: Composant1.A3, PC_Fan.pin2, R2.Pin_1
  GND: Composant1.GND, PIR1.GND, DHT1.GND, PC_Fan.pin4, R3.Pin_1, M1.Pin_2, M1.Pin_4, Composant2.VSS
  5V: Composant1.VIN, PIR1.VDD, M1.Pin_3, Composant2.VDD
  N3: Composant1.D0, PC_Fan.pin3
  N4: Composant1.D1, Composant2.DIN
  N5: Composant1.D4, PIR1.SIG
  N6: Composant1.D5, DHT1.DATA, R1.Pin_1
  3.3V: Composant1.3V3, DHT1.VDD, R1.Pin_0, LDR.pin_1, R2.Pin_0
  12V: PC_Fan.pin1, M1.Pin_1
